// Logisim project adder.circ as structural Verilog
module HalfAdder (
  input  A,
  input  B,
  output S,
  output Cout
);

  xor xor_1 (S, A, B);
  and and_1 (Cout, A, B);
endmodule

module FullAdder (
  input  A,
  input  B,
  input  Cin,
  output S,
  output Cout
);

  wire halfadder_1_cout, halfadder_1_s, halfadder_2_cout;

  HalfAdder halfadder_1 (.A(B), .B(Cin), .S(halfadder_1_s), .Cout(halfadder_1_cout));
  HalfAdder halfadder_2 (.A(A), .B(halfadder_1_s), .S(S), .Cout(halfadder_2_cout));
  or or_1 (Cout, halfadder_2_cout, halfadder_1_cout);
endmodule

module _4bit_CPA (
  input  A_0,
  input  A_1,
  input  A_2,
  input  A_3,
  input  B_0,
  input  B_1,
  input  B_2,
  input  B_3,
  output overflow,
  output S_0,
  output S_1,
  output S_2,
  output S_3
);

  wire fulladder_1_cout, fulladder_2_cout, fulladder_3_cout;

  FullAdder fulladder_1 (.A(A_0), .B(B_0), .Cin(1'b0), .S(S_0), .Cout(fulladder_1_cout));
  FullAdder fulladder_2 (.A(A_1), .B(B_1), .Cin(fulladder_1_cout), .S(S_1), .Cout(fulladder_2_cout));
  FullAdder fulladder_3 (.A(A_2), .B(B_2), .Cin(fulladder_2_cout), .S(S_2), .Cout(fulladder_3_cout));
  FullAdder fulladder_4 (.A(A_3), .B(B_3), .Cin(fulladder_3_cout), .S(S_3), .Cout(overflow));
endmodule

module _2bit_RCA (
  input  Cin,
  input  A_0,
  input  B,
  input  Cin_2,
  input  B_0,
  input  A_1,
  input  B_2,
  input  B_1,
  output S_0,
  output Cout,
  output S,
  output Cout_2,
  output S_1,
  output Cout_3,
  output Cout_4,
  output S_2,
  output Cout_5,
  output Cout_6
);

  xor xor_1 (B, A_0, B_0);
  and and_1 (Cout_3, A_0, B_0);
  xor xor_2 (S_0, Cin, B);
  and and_2 (Cout, Cin, B);
  and and_3 (Cout_6, A_1, B_1);
  or or_1 (Cin_2, Cout, Cout_3);
  xor xor_3 (B_2, A_1, B_1);
  xor xor_4 (S_1, Cin_2, B_2);
  and and_4 (Cout_4, Cin_2, B_2);
  or or_2 (Cout_5, Cout_4, Cout_6);

  assign Cout_2 = Cin_2;
  assign S = B;
  assign S_2 = B_2;

  // Notes on the sheet:
  //   P0
  //   G0
  //   P1
  //   G1
endmodule

module FullAdder_flat (
  input  Cin,
  input  A,
  input  B,
  input  B_2,
  output S,
  output Cout,
  output S_2,
  output Cout_2,
  output Cout_3
);

  xor xor_1 (B, A, B_2);
  and and_1 (Cout_3, A, B_2);
  xor xor_2 (S, Cin, B);
  and and_2 (Cout, Cin, B);
  or or_1 (Cout_2, Cout, Cout_3);

  assign S_2 = B;

  // Notes on the sheet:
  //   P
  //   G
endmodule

module CLA (
  input  P0,
  input  P1,
  input  G1,
  input  P1_2,
  input  P0_2,
  input  Cin,
  output Cout1
);

  wire and_1_out, and_2_out, and_3_out, or_1_out;

  and and_1 (and_1_out, P0, P1);
  and and_2 (and_2_out, P1_2, P0_2);
  or or_1 (or_1_out, and_1_out, G1);
  and and_3 (and_3_out, and_2_out, Cin);
  or or_2 (Cout1, or_1_out, and_3_out);
endmodule
