// Logisim project comparators.circ as structural Verilog: 3 circuits, main circuit main
module main (
  input  [3:0] A,
  input  [3:0] B,
  output NEQ,
  output EQ,
  output GE,
  output LT,
  output LE,
  output GT
);

  EQ eq_1 (.A(A), .B(B), .Y(EQ));
  LT lt_1 (.A(A), .B(B), .Y(LT));
  LT lt_2 (.A(B), .B(A), .Y(GT));
  not not_1 (NEQ, EQ);
  not not_2 (GE, LT);
  not not_3 (LE, GT);
endmodule

module EQ (
  input  [3:0] A,
  input  [3:0] B,
  output Y
);

  wire [3:0] xnor_1_out;

  assign xnor_1_out = ~(A ^ B);  // XNOR_Gate xnor_1, 4 bits wide
  and and_1 (Y, xnor_1_out[0], xnor_1_out[1], xnor_1_out[2], xnor_1_out[3]);
endmodule

module LT (
  input  [3:0] A,
  input  [3:0] B,
  output Y
);

  wire [2:0] subtractor_1_out;

  Subtractor #(.width(4)) subtractor_1 (.a(A), .b(B), .out({Y, subtractor_1_out}));  // open: bin, bout
endmodule
