// Logisim project latch_and_flip_flop.circ as structural Verilog
module not_not (
);

  wire not_1_out, not_2_out;

  not not_1 (not_1_out, not_2_out);
  not not_2 (not_2_out, not_1_out);
endmodule

module SR_Latch (
  input  R,
  input  S,
  output Q,
  output nQ
);

  nor nor_1 (Q, nQ, R);
  nor nor_2 (nQ, Q, S);
endmodule

module D_Latch (
  input  CLK,
  input  D,
  output Q
);

  wire and_1_out, and_2_out, not_1_out;

  not not_1 (not_1_out, D);
  and and_1 (and_1_out, CLK, not_1_out);
  and and_2 (and_2_out, CLK, D);
  SR_Latch sr_latch_1 (.R(and_1_out), .S(and_2_out), .Q(Q));  // open: nQ
endmodule

module D_FlipFlop (
  input  CLK,
  input  D,
  output Q
);

  wire d_latch_1_q, not_1_out;

  not not_1 (not_1_out, CLK);
  D_Latch d_latch_1 (.CLK(not_1_out), .D(D), .Q(d_latch_1_q));
  D_Latch d_latch_2 (.CLK(CLK), .D(d_latch_1_q), .Q(Q));

  // Notes on the sheet:
  //   master
  //   slave
endmodule

module EnabledDFF (
  input  CLK,
  input  D,
  input  EN,
  output Q
);

  wire and_1_out;

  and and_1 (and_1_out, D, EN);
  D_FlipFlop d_flipflop_1 (.D(and_1_out), .Q(Q), .CLK(CLK));
endmodule

module wrong (
  input  CLK,
  input  EN,
  input  D,
  output Q
);

  wire and_1_out;

  and and_1 (and_1_out, CLK, EN);
  D_FlipFlop d_flipflop_1 (.D(D), .Q(Q), .CLK(and_1_out));
endmodule

module ResetDFF (
  input  CLK,
  input  D,
  input  RESET,
  output Q
);

  wire and_1_out;

  and and_1 (and_1_out, D, RESET);
  D_FlipFlop d_flipflop_1 (.D(and_1_out), .Q(Q), .CLK(CLK));
endmodule
