// Logisim project logic_gates.circ as structural Verilog
module NAND (
  input  A,
  input  B,
  output Y
);

  nand nand_1 (Y, A, B);
endmodule

module AND_by_NAND (
  input  A,
  input  B,
  output Y
);

  wire nand_1_out;

  nand nand_1 (nand_1_out, A, B);
  not not_1 (Y, nand_1_out);
endmodule

module NOT_by_NAND (
  input  A,
  output Y
);

  nand nand_1 (Y, A, A);

  // Notes on the sheet:
  //   B
endmodule

module NOT (
  input  in_1,
  output out_2
);

  not not_1 (out_2, in_1);
endmodule

module AND (
  input  in_1,
  input  in_2,
  output out_3
);

  and and_1 (out_3, in_1, in_2);
endmodule

module OR_by_NAND (
  input  A,
  input  B,
  output Y
);

  wire not_1_out, not_2_out;

  not not_1 (not_1_out, A);
  not not_2 (not_2_out, B);
  nand nand_1 (Y, not_1_out, not_2_out);
endmodule

module OR (
  input  in_1,
  input  in_2,
  output out_3
);

  or or_1 (out_3, in_1, in_2);
endmodule

module XOR_by_NAND (
  input  in_1,
  input  in_2,
  output out_3
);

  wire and_1_out, and_2_out, not_1_out, not_2_out;

  not not_1 (not_1_out, in_2);
  not not_2 (not_2_out, in_1);
  and and_1 (and_1_out, in_1, not_1_out);
  and and_2 (and_2_out, not_2_out, in_2);
  or or_1 (out_3, and_1_out, and_2_out);
endmodule

module XOR (
  input  in_1,
  input  in_2,
  output out_3
);

  xor xor_1 (out_3, in_1, in_2);
endmodule
