// Logisim project mux.circ as structural Verilog
module _2_1MUX (
  input  A,
  input  B,
  input  sel,
  output Y
);

  wire and_1_out, and_2_out, not_1_out;

  and and_1 (and_1_out, A, not_1_out);
  not not_1 (not_1_out, sel);
  and and_2 (and_2_out, B, sel);
  or or_1 (Y, and_1_out, and_2_out);
endmodule

module _1_2DEMUX (
  input  Y,
  input  sel,
  output A,
  output B
);

  wire not_1_out;

  not not_1 (not_1_out, sel);
  and and_1 (A, Y, not_1_out);
  and and_2 (B, Y, sel);
endmodule
