// Logisim project pc.circ as structural Verilog: 1 circuit, main circuit main
module main (
  input  [7:0] in_1,
  input  in_2,
  output [7:0] PC
);

  wire button_1_out;
  wire [7:0] adder_1_out, multiplexer_1_out;

  Adder adder_1 (.a(PC), .b(8'h4), .out(adder_1_out));  // open: cin, cout
  Multiplexer #(.width(8), .enable("false")) multiplexer_1 (
    .in0(adder_1_out), .in1(in_1), .out(multiplexer_1_out), .sel(in_2));
  Button button_1 (.out(button_1_out));
  Register register_1 (.D(multiplexer_1_out), .Q(PC), .clk(button_1_out));  // open: en, clr
  ROM rom_1 (.addr(PC));  // open: data, sel
endmodule
