// Logisim project tracfic_light.circ as structural Verilog: 1 circuit, main circuit main
module main (
);

  wire button_1_out, demultiplexer_1_out0, demultiplexer_1_out1, demultiplexer_1_out2, demultiplexer_1_out3,
       demultiplexer_2_out0, demultiplexer_2_out1, demultiplexer_2_out2, demultiplexer_2_out3, or_1_out,
       or_2_out;
  wire [1:0] adder_1_out, register_1_q;

  LED led_1 (.in(or_1_out));
  LED led_2 (.in(demultiplexer_1_out1));
  LED led_3 (.in(demultiplexer_1_out0));
  or or_1 (or_1_out, demultiplexer_1_out2, demultiplexer_1_out3);
  Adder #(.width(2)) adder_1 (.a(2'b00), .b(register_1_q), .out(adder_1_out), .cin(1'b1));  // open: cout
  Button button_1 (.out(button_1_out));
  Demultiplexer #(.select(2), .enable("false")) demultiplexer_1 (
    .out0(demultiplexer_1_out0), .out1(demultiplexer_1_out1), .out2(demultiplexer_1_out2),
    .out3(demultiplexer_1_out3), .in(1'b1), .sel(register_1_q));
  Register #(.width(2)) register_1 (.D(adder_1_out), .Q(register_1_q), .clk(button_1_out));  // open: en, clr
  Demultiplexer #(.select(2), .enable("false")) demultiplexer_2 (
    .out0(demultiplexer_2_out0), .out1(demultiplexer_2_out1), .out2(demultiplexer_2_out2),
    .out3(demultiplexer_2_out3), .in(1'b1), .sel(register_1_q));
  or or_2 (or_2_out, demultiplexer_2_out0, demultiplexer_2_out1);
  LED led_4 (.in(or_2_out));
  LED led_5 (.in(demultiplexer_2_out2));
  LED led_6 (.in(demultiplexer_2_out3));
endmodule
